# Fritzing sketch Alarm System (saved by Fritzing 0.9.9b)
breadboards: 2

parts:
  Argon1 = Particle Argon
  J1 = Piezo Speaker
  PIR1 = PIR sensor

nets:
  3.3V: Argon1.3.3V, PIR1.VDD
  GND: Argon1.GND, J1.pin2, PIR1.GND
  N1: Argon1.D5, PIR1.SIG
  N2: Argon1.D7, J1.pin1

custom parts:
  Particle Argon: The Argon is a powerful Wi-Fi enabled development board that can act as either a standalone Wi-Fi endpoint or Wi-Fi enabled gateway for Particle Mesh networks. It is based on the Nordic nRF52840 and has built-in battery charging circuitry so it’s easy to connect a Li-Po and deploy your local network in minutes. The Argon is great for connecting existing projects to the Particle Device Cloud or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
